// Logisim project control_logic.circ as structural Verilog: 1 circuit, main circuit control_logic
module control_logic (
  input  [31:0] inst,
  input  BrEq,
  input  BrLt,
  output PCSel,
  output RegWEn,
  output [2:0] ImmSel,
  output BrUn,
  output ASel,
  output BSel,
  output [3:0] ALUSel,
  output MemRW,
  output [1:0] WBSel,
  output CSRSel,
  output CSRWen
);

  wire and_1_out, and_2_out, and_3_out, and_4_out, and_5_out, and_6_out, and_7_out, and_8_out, and_9_out,
       and_10_out, and_11_out, and_12_out, and_13_out, and_14_out, and_15_out, and_16_out, and_17_out,
       and_18_out, and_19_out, and_20_out, and_21_out, auipc, comparator_11_eq, comparator_12_eq,
       comparator_13_eq, comparator_14_eq, comparator_15_eq, comparator_16_eq, comparator_17_eq,
       comparator_18_eq, comparator_19_eq, comparator_20_eq, comparator_21_eq, comparator_22_eq,
       comparator_23_eq, comparator_24_eq, comparator_25_eq, comparator_26_eq, comparator_27_eq,
       comparator_28_eq, comparator_29_eq, comparator_30_eq, comparator_31_eq, comparator_32_eq,
       comparator_33_eq, comparator_34_eq, comparator_35_eq, comparator_36_eq, CsrWrite, IArth, IType, jalr,
       LoadType, lui, not_1_out, not_2_out, not_3_out, not_4_out, or_3_out, or_4_out, or_5_out, or_6_out,
       or_7_out, or_8_out, or_9_out, or_10_out, or_11_out, or_12_out, or_13_out, or_14_out, or_15_out,
       or_16_out, or_17_out, or_18_out, RType, SBType, SType, UJType, UType;

  Comparator #(.width(7)) comparator_1 (.a(inst[6:0]), .b(7'b0000011), .eq(LoadType));  // open: gt, lt
  Comparator #(.width(7)) comparator_2 (.a(inst[6:0]), .b(7'b0010011), .eq(IArth));  // open: gt, lt
  Comparator #(.width(7)) comparator_3 (.a(inst[6:0]), .b(7'b1100111), .eq(jalr));  // open: gt, lt
  Comparator #(.width(7)) comparator_4 (.a(inst[6:0]), .b(7'b1110011), .eq(CsrWrite));  // open: gt, lt
  Comparator #(.width(7)) comparator_5 (.a(inst[6:0]), .b(7'b0100011), .eq(SType));  // open: gt, lt
  Comparator #(.width(7)) comparator_6 (.a(inst[6:0]), .b(7'b1100011), .eq(SBType));  // open: gt, lt
  Comparator #(.width(7)) comparator_7 (.a(inst[6:0]), .b(7'b0010111), .eq(auipc));  // open: gt, lt
  Comparator #(.width(7)) comparator_8 (.a(inst[6:0]), .b(7'b0110111), .eq(lui));  // open: gt, lt
  Comparator #(.width(7)) comparator_9 (.a(inst[6:0]), .b(7'b1101111), .eq(UJType));  // open: gt, lt
  Comparator #(.width(7)) comparator_10 (.a(inst[6:0]), .b(7'b0110011), .eq(RType));  // open: gt, lt
  or or_1 (UType, auipc, lui);
  or or_2 (IType, LoadType, IArth, jalr, CsrWrite);
  assign ImmSel = IType ? 3'b000 : 3'bz;  // Controlled_Buffer controlled_buffer_1
  assign ImmSel = SType ? 3'b001 : 3'bz;  // Controlled_Buffer controlled_buffer_2
  assign ImmSel = SBType ? 3'b010 : 3'bz;  // Controlled_Buffer controlled_buffer_3
  assign ImmSel = UType ? 3'b011 : 3'bz;  // Controlled_Buffer controlled_buffer_4
  assign ImmSel = UJType ? 3'b100 : 3'bz;  // Controlled_Buffer controlled_buffer_5
  or or_3 (or_3_out, IType, RType);
  assign ASel = or_3_out ? 1'b0 : 1'bz;  // Controlled_Buffer controlled_buffer_6
  assign ASel = auipc ? 1'b1 : 1'bz;  // Controlled_Buffer controlled_buffer_7
  buf or_4 (or_4_out, RType);  // OR_Gate
  assign BSel = or_4_out ? 1'b0 : 1'bz;  // Controlled_Buffer controlled_buffer_8
  assign BSel = or_5_out ? 1'b1 : 1'bz;  // Controlled_Buffer controlled_buffer_9
  or or_5 (or_5_out, UJType, UType, IType, SType, SBType);
  assign PCSel = or_6_out ? 1'b1 : 1'bz;  // Controlled_Buffer controlled_buffer_10
  or or_6 (or_6_out, SBType, jalr, SBType, UJType, UJType);
  not not_1 (not_1_out, or_6_out);
  assign PCSel = not_1_out ? 1'b0 : 1'bz;  // Controlled_Buffer controlled_buffer_11
  not not_2 (not_2_out, CsrWrite);
  assign CSRWen = 1'b1 ? CsrWrite : 1'bz;  // Controlled_Buffer controlled_buffer_12
  assign CSRWen = 1'b0 ? not_2_out : 1'bz;  // Controlled_Buffer controlled_buffer_13
  assign RegWEn = not_3_out ? 1'b0 : 1'bz;  // Controlled_Buffer controlled_buffer_14
  not not_3 (not_3_out, or_7_out);
  or or_7 (or_7_out, IType, UType, UJType, RType);
  not not_4 (not_4_out, SType);
  assign RegWEn = or_7_out ? 1'b1 : 1'bz;  // Controlled_Buffer controlled_buffer_15
  Comparator #(.width(3)) comparator_11 (.a(inst[14:12]), .b(3'b001), .eq(comparator_11_eq));  // open: gt, lt
  assign CSRSel = comparator_11_eq ? 1'b1 : 1'bz;  // Controlled_Buffer controlled_buffer_16
  assign CSRSel = comparator_12_eq ? 1'b0 : 1'bz;  // Controlled_Buffer controlled_buffer_17
  Comparator #(.width(3)) comparator_12 (.a(inst[14:12]), .b(3'b101), .eq(comparator_12_eq));  // open: gt, lt
  or or_8 (or_8_out, IArth, UType, CsrWrite, RType);
  assign WBSel = or_8_out ? 2'b01 : 2'bz;  // Controlled_Buffer controlled_buffer_18
  assign WBSel = LoadType ? 2'b00 : 2'bz;  // Controlled_Buffer controlled_buffer_19
  assign WBSel = or_9_out ? 2'b10 : 2'bz;  // Controlled_Buffer controlled_buffer_20
  or or_9 (or_9_out, jalr, UJType);
  assign MemRW = 1'b1 ? SType : 1'bz;  // Controlled_Buffer controlled_buffer_21
  assign MemRW = 1'b0 ? not_4_out : 1'bz;  // Controlled_Buffer controlled_buffer_22
  and and_1 (and_1_out, RType, comparator_13_eq);
  Comparator #(.width(7)) comparator_13 (.a(inst[31:25]), .b({7{1'b0}}), .eq(comparator_13_eq));  // open: gt, lt
  and and_2 (and_2_out, RType, comparator_14_eq);
  Comparator #(.width(7)) comparator_14 (.a(inst[31:25]), .b({7{1'b0}}), .eq(comparator_14_eq));  // open: gt, lt
  and and_3 (and_3_out, RType, comparator_15_eq);
  Comparator #(.width(7)) comparator_15 (.a(inst[31:25]), .b({7{1'b0}}), .eq(comparator_15_eq));  // open: gt, lt
  and and_4 (and_4_out, RType, comparator_16_eq);
  Comparator #(.width(7)) comparator_16 (.a(inst[31:25]), .b({7{1'b0}}), .eq(comparator_16_eq));  // open: gt, lt
  or or_10 (or_10_out, IArth, and_1_out);
  Comparator #(.width(3)) comparator_17 (.a(inst[14:12]), .b(3'b100), .eq(comparator_17_eq));  // open: gt, lt
  or or_11 (or_11_out, IArth, and_2_out);
  Comparator #(.width(3)) comparator_18 (.a(inst[14:12]), .b(3'b110), .eq(comparator_18_eq));  // open: gt, lt
  or or_12 (or_12_out, IArth, and_3_out);
  Comparator #(.width(3)) comparator_19 (.a(inst[14:12]), .b(3'b111), .eq(comparator_19_eq));  // open: gt, lt
  or or_13 (or_13_out, IArth, and_4_out);
  Comparator #(.width(3)) comparator_20 (.a(inst[14:12]), .b(3'b010), .eq(comparator_20_eq));  // open: gt, lt
  and and_5 (and_5_out, or_10_out, comparator_17_eq);
  assign ALUSel = and_5_out ? 4'b0011 : 4'bz;  // Controlled_Buffer controlled_buffer_23
  and and_6 (and_6_out, or_11_out, comparator_18_eq);
  assign ALUSel = and_6_out ? 4'b0010 : 4'bz;  // Controlled_Buffer controlled_buffer_24
  and and_7 (and_7_out, or_12_out, comparator_19_eq);
  assign ALUSel = and_7_out ? 4'b0001 : 4'bz;  // Controlled_Buffer controlled_buffer_25
  and and_8 (and_8_out, or_13_out, comparator_20_eq);
  assign ALUSel = and_8_out ? 4'b0111 : 4'bz;  // Controlled_Buffer controlled_buffer_26
  and and_9 (and_9_out, RType, comparator_21_eq);
  Comparator #(.width(7)) comparator_21 (.a(inst[31:25]), .b({7{1'b0}}), .eq(comparator_21_eq));  // open: gt, lt
  or or_14 (or_14_out, IArth, and_9_out);
  Comparator #(.width(3)) comparator_22 (.a(inst[14:12]), .b(3'b000), .eq(comparator_22_eq));  // open: gt, lt
  or or_15 (or_15_out, IArth, RType);
  and and_10 (and_10_out, or_15_out, comparator_23_eq, comparator_24_eq);
  Comparator #(.width(7)) comparator_23 (.a(inst[31:25]), .b({7{1'b0}}), .eq(comparator_23_eq));  // open: gt, lt
  Comparator #(.width(3)) comparator_24 (.a(inst[14:12]), .b(3'b101), .eq(comparator_24_eq));  // open: gt, lt
  or or_16 (or_16_out, IArth, RType);
  and and_11 (and_11_out, or_16_out, comparator_25_eq, comparator_26_eq);
  Comparator #(.width(7)) comparator_25 (.a(inst[31:25]), .b(7'b0100000), .eq(comparator_25_eq));  // open: gt, lt
  Comparator #(.width(3)) comparator_26 (.a(inst[14:12]), .b(3'b101), .eq(comparator_26_eq));  // open: gt, lt
  or or_17 (or_17_out, IArth, RType);
  and and_12 (and_12_out, or_17_out, comparator_27_eq, comparator_28_eq);
  Comparator #(.width(7)) comparator_27 (.a(inst[31:25]), .b({7{1'b0}}), .eq(comparator_27_eq));  // open: gt, lt
  Comparator #(.width(3)) comparator_28 (.a(inst[14:12]), .b(3'b001), .eq(comparator_28_eq));  // open: gt, lt
  and and_13 (and_13_out, or_14_out, comparator_22_eq);
  assign ALUSel = and_10_out ? 4'b0100 : 4'bz;  // Controlled_Buffer controlled_buffer_27
  assign ALUSel = and_11_out ? 4'b0101 : 4'bz;  // Controlled_Buffer controlled_buffer_28
  assign ALUSel = and_12_out ? 4'b0110 : 4'bz;  // Controlled_Buffer controlled_buffer_29
  or or_18 (or_18_out, auipc, SType, LoadType, and_13_out, SBType, UJType, jalr);
  assign ALUSel = or_18_out ? 4'b0000 : 4'bz;  // Controlled_Buffer controlled_buffer_30
  assign ALUSel = lui ? 4'b1101 : 4'bz;  // Controlled_Buffer controlled_buffer_31
  Comparator #(.width(7)) comparator_29 (.a(inst[31:25]), .b(7'b0000001), .eq(comparator_29_eq));  // open: gt, lt
  Comparator #(.width(7)) comparator_30 (.a(inst[31:25]), .b(7'b0100000), .eq(comparator_30_eq));  // open: gt, lt
  Comparator #(.width(7)) comparator_31 (.a(inst[31:25]), .b(7'b0000001), .eq(comparator_31_eq));  // open: gt, lt
  Comparator #(.width(7)) comparator_32 (.a(inst[31:25]), .b(7'b0000001), .eq(comparator_32_eq));  // open: gt, lt
  and and_14 (and_14_out, RType, comparator_29_eq);
  and and_15 (and_15_out, and_14_out, comparator_33_eq);
  Comparator #(.width(3)) comparator_33 (.a(inst[14:12]), .b(3'b000), .eq(comparator_33_eq));  // open: gt, lt
  and and_16 (and_16_out, RType, comparator_30_eq);
  and and_17 (and_17_out, and_16_out, comparator_34_eq);
  Comparator #(.width(3)) comparator_34 (.a(inst[14:12]), .b(3'b000), .eq(comparator_34_eq));  // open: gt, lt
  and and_18 (and_18_out, RType, comparator_31_eq);
  and and_19 (and_19_out, and_18_out, comparator_35_eq);
  Comparator #(.width(3)) comparator_35 (.a(inst[14:12]), .b(3'b001), .eq(comparator_35_eq));  // open: gt, lt
  and and_20 (and_20_out, RType, comparator_32_eq);
  and and_21 (and_21_out, and_20_out, comparator_36_eq);
  Comparator #(.width(3)) comparator_36 (.a(inst[14:12]), .b(3'b011), .eq(comparator_36_eq));  // open: gt, lt
  assign ALUSel = and_15_out ? 4'b1010 : 4'bz;  // Controlled_Buffer controlled_buffer_32
  assign ALUSel = and_17_out ? 4'b1100 : 4'bz;  // Controlled_Buffer controlled_buffer_33
  assign ALUSel = and_19_out ? 4'b1110 : 4'bz;  // Controlled_Buffer controlled_buffer_34
  assign ALUSel = and_21_out ? 4'b1011 : 4'bz;  // Controlled_Buffer controlled_buffer_35

  // Other names for the same wires on the sheet: opcode[6:0] = inst[6:0]; rd[4:0] = inst[11:7];
  //   funct3[2:0] = inst[14:12]; rs1[4:0] = inst[19:15]; rs2[4:0] = inst[24:20]; funct7[6:0] = inst[31:25]

  // Notes on the sheet:
  //   INPUTS to your circuit
  //   not implemented
  //   not implemented
  //   not implemented
  //   DON'T CHANGE THE LOCATIONS OF THE INPUTS AND OUTPUTS!
  //   OUTPUT from your circuit
  //   0 for rs1, 1 for PC
  //   lui will use ALU's Bsel
  //   0 for rs2, 1 for imm_gen
  //   xor
  //   or
  //   and
  //   slt
  //   add
  //   srl
  //   sra
  //   sll
  //   mul
  //   sub
  //   mulh
  //   mulhu
endmodule
