// Logisim project cpu.circ as structural Verilog: 1 circuit, main circuit cpu
module cpu (
  input  clk,
  input  [31:0] INSTRUCTION,
  input  [31:0] READ_DATA,
  output [31:0] WRITE_ADDRESS,
  output [31:0] PROGRAM_COUNTER,
  output [31:0] ra,
  output [31:0] sp,
  output [31:0] t0,
  output [31:0] t1,
  output [31:0] t2,
  output [31:0] s0,
  output [31:0] s1,
  output [31:0] a0,
  output [31:0] tohost,
  output [3:0] WRITE_ENABLE,
  output [31:0] WRITE_DATA
);

  wire ASel, BeEq, BrLt, BrUn, BSel, CSRSel, MemRW, PCSel, RWE;
  wire [1:0] WBSel;
  wire [2:0] funct3, ImmSel;
  wire [3:0] ALUSel;
  wire [6:0] funct7, opcode;
  wire [24:7] Phase2_Inst;
  wire [31:0] adder_1_out, Generated_imm, multiplexer_1_out, multiplexer_2_out, multiplexer_3_out, Phase2_PC,
       rs_1, Writeback_Data;

  Adder #(.width(32)) adder_1 (.a(PROGRAM_COUNTER), .b(32'h4), .out(adder_1_out));  // open: cin, cout
  Multiplexer #(.enable("false"), .width(32)) multiplexer_1 (
    .in0(adder_1_out), .in1(WRITE_ADDRESS), .out(multiplexer_1_out), .sel(PCSel));
  Register #(.width(32)) PC (.D(multiplexer_1_out), .clk(clk), .Q(PROGRAM_COUNTER));  // open: en, clr
  Register #(.width(32)) Pipeline_PC_Reg (.D(PROGRAM_COUNTER), .en(1'b1), .clk(clk), .Q(Phase2_PC));  // open: clr
  Register #(.width(32)) Pipeline_Inst_Reg (
    .D(INSTRUCTION), .en(1'b1), .clk(clk), .Q({funct7, Phase2_Inst[24:15], funct3, Phase2_Inst[11:7], opcode}));  // open: clr
  control_logic control_logic_1 (
    .CSRWen(CSRSel), .PCSel(PCSel), .RegWEn(RWE), .ImmSel(ImmSel), .BrUn(BrUn), .ASel(ASel), .BSel(BSel),
    .ALUSel(ALUSel), .MemRW(MemRW), .WBSel(WBSel), .CSRSel(CSRSel),
    .inst({funct7, Phase2_Inst[24:15], funct3, Phase2_Inst[11:7], opcode}), .BrEq(BeEq), .BrLt(BrLt));
  regfile regfile_1 (
    .rs1(Phase2_Inst[19:15]), .rs2(Phase2_Inst[24:20]), .rd(Phase2_Inst[11:7]), .Write_Data(Writeback_Data),
    .RegWEn(RWE), .clk(clk), .ra(ra), .sp(sp), .t0(t0), .t1(t1), .t2(t2), .s0(s0), .s1(s1), .a0(a0),
    .Read_Data_1(rs_1), .Read_Data_2(WRITE_DATA));
  imm_gen imm_gen_1 (
    .inst({funct7, Phase2_Inst[24:15], funct3, Phase2_Inst[11:7], opcode}), .ImmSel(ImmSel),
    .imm(Generated_imm));
  Multiplexer #(.enable("false"), .width(32)) multiplexer_2 (
    .in0(rs_1), .in1(Phase2_PC), .out(multiplexer_2_out), .sel(ASel));
  Multiplexer #(.enable("false"), .width(32)) multiplexer_3 (
    .in0(WRITE_DATA), .in1(Generated_imm), .out(multiplexer_3_out), .sel(BSel));
  alu alu_1 (.Result(WRITE_ADDRESS), .A(multiplexer_2_out), .B(multiplexer_3_out), .ALUSel(ALUSel));
  branch_comp branch_comp_1 (.rs1(rs_1), .rs2(WRITE_DATA), .BrUn(BrUn), .BrEq(BrLt), .BrLt(BeEq));
  csr csr_1 (.tohost(tohost));  // open: CSR_address, CSR_din, CSR_WE, clk
  Multiplexer #(.enable("false"), .select(2), .width(32)) multiplexer_4 (
    .in0(READ_DATA), .in1(WRITE_ADDRESS), .in2(PROGRAM_COUNTER), .out(Writeback_Data), .sel(WBSel));  // open: in3

  // Other names for the same wires on the sheet: ALU_Output[31:0] = WRITE_ADDRESS;
  //   Phase2_Inst (some bits) = {funct7, funct3, opcode}; rd[4:0] = Phase2_Inst[11:7]; rs1[4:0] = Phase2_Inst[19:15];
  //   rs2[4:0] = Phase2_Inst[24:20]; rs_2[31:0] = WRITE_DATA

  // Notes on the sheet:
  //   Output to IMEM
  //   IMEM (do **NOT** move this)
  //   Inputs from IMEM
  //   It is OK to move the PC, RegFile, ALU, MEM, Branch Comp, Imm Gen, and Control Logic to wherever is most convenient for you when constructing your CPU, and to delete this text
  //   Inputs/Outputs for testing. Do **NOT** move these.
  //   Outputs To DMEM
  //   DMEM (do **NOT** move this)
  //   Inputs From DMEM
  //   pesudo DMEM
endmodule
